# Fritzing sketch bancTeste (saved by Fritzing 0.9.3b)
breadboards: 1

parts:
  LCM1602_IIC1 = LCM1602 IIC [part_number="LCM1602 IIC" chip_label="LCM1602 IIC" package="DIP (Dual Inline) [THT]"]
  Part1 = Arduino Uno (Rev3) - ICSP
  LCD1 = LCD screen
  Mod1 = Full Size SD Card Module
  S1 = Pushbutton [package="[THT]"]
  S2 = SWITCH-MOMENTARY-2 [package=tactile-switch-1101ne]
  HC-SR04_Sensor_1 = HC-SR04 Ultrasonic Distance Sensor

nets:
  VSS: LCM1602_IIC1.VSS, LCD1.VSS
  VDD: LCM1602_IIC1.VDD, LCD1.VDD
  N1: LCM1602_IIC1.V0, LCD1.V0
  N2: LCM1602_IIC1.RS, LCD1.RS
  N3: LCM1602_IIC1.RW, LCD1.R/W
  N4: LCM1602_IIC1.E, LCD1.E
  N5: LCM1602_IIC1.D0, LCD1.DB0
  N6: LCM1602_IIC1.D1, LCD1.DB1
  N7: LCM1602_IIC1.D2, LCD1.DB2
  N8: LCM1602_IIC1.D3, LCD1.DB3
  N9: LCM1602_IIC1.D4, LCD1.DB4
  N10: LCM1602_IIC1.D5, LCD1.DB5
  N11: LCM1602_IIC1.D6, LCD1.DB6
  N12: LCM1602_IIC1.D7, LCD1.DB7
  N13: LCM1602_IIC1.A, LCD1.LED+
  N14: LCM1602_IIC1.K, LCD1.LED-
  GND: LCM1602_IIC1.GND, Part1.GND, Mod1.pin_1, Mod1.pin_2, S1.Pin_1, S1.Pin_2, S2.1, HC-SR04_Sensor_1.GND
  VCC: LCM1602_IIC1.VCC, Part1.5V, Mod1.pin_6, HC-SR04_Sensor_1.VCC
  N15: LCM1602_IIC1.SDA, Part1.A4/SDA
  N16: LCM1602_IIC1.SCL, Part1.A5/SCL
  N17: Part1.D10_PWM/SS, Mod1.pin_8
  N18: Part1.D11_PWM/MOSI, Mod1.pin_10
  N19: Part1.D12/MISO, Mod1.pin_14
  N20: Part1.D13/SCK, Mod1.pin_12
  N21: Part1.D2, S2.2
  N22: Part1.D3_PWM, S1.Pin_3
  N23: Part1.D5_PWM, HC-SR04_Sensor_1.ECHO
  N24: Part1.D6_PWM, HC-SR04_Sensor_1.TRIG

custom parts:
  LCM1602 IIC: I2C-Module to use a 1602 or 2004 LCD on with the wire.h libory Serial LCD Modul
  Full Size SD Card Module: SD Card Module Slot Socket Reader For Arduino ARM MCU
